// Logisim project ADD&SUB.circ as structural Verilog: 1 circuit, main circuit main
module main (
  input  A,
  input  a2,
  input  a1,
  input  a0,
  input  [3:0] in_5,
  input  in_6,
  input  in_7,
  input  in_8,
  input  in_9,
  input  b3,
  input  b2,
  input  b1,
  input  b0,
  input  [3:0] in_14,
  input  Selector,
  output out_16,
  output out_17,
  output C0_out,
  output C1_out,
  output out_20,
  output C3_out
);

  wire and_1_out, and_2_out, and_3_out, and_4_out, and_5_out, and_6_out, and_7_out, and_8_out, and_9_out,
       and_10_out, and_11_out, not_1_out, not_3_out, not_4_out, xor_1_out, xor_2_out, xor_3_out, xor_4_out;
  wire [3:0] multiplexer_1_out, not_2_out, xor_5_out;

  and and_1 (and_1_out, not_1_out, C3_out);
  LED led_1 (.in(and_1_out));
  not not_1 (not_1_out, Selector);
  Multiplexer #(.width(4), .enable("false")) multiplexer_1 (
    .in0(in_14), .in1(not_2_out), .out(multiplexer_1_out), .sel(Selector));
  assign not_2_out = ~in_14;  // NOT_Gate not_2, 4 bits wide
  and and_2 (and_2_out, in_5[0], multiplexer_1_out[0]);
  and and_3 (and_3_out, in_5[2], multiplexer_1_out[2]);
  and and_4 (and_4_out, in_5[3], multiplexer_1_out[3]);
  xor xor_1 (xor_1_out, in_5[0], multiplexer_1_out[0]);
  xor xor_2 (xor_2_out, in_5[1], multiplexer_1_out[1]);
  and and_5 (and_5_out, in_5[1], multiplexer_1_out[1]);
  xor xor_3 (xor_3_out, in_5[2], multiplexer_1_out[2]);
  xor xor_4 (xor_4_out, in_5[3], multiplexer_1_out[3]);
  not not_3 (not_3_out, in_6);
  not not_4 (not_4_out, in_9);
  and and_6 (and_6_out, not_3_out, in_9);
  and and_7 (and_7_out, in_6, not_4_out);
  or or_1 (out_16, and_6_out, and_7_out);
  xor xor_5 (xor_5_out[0], Selector, xor_1_out);
  and and_8 (and_8_out, xor_1_out, Selector);
  xor xor_6 (xor_5_out[1], C0_out, xor_2_out);
  and and_9 (and_9_out, xor_2_out, C0_out);
  xor xor_7 (xor_5_out[2], C1_out, xor_3_out);
  and and_10 (and_10_out, xor_3_out, C1_out);
  xor xor_8 (xor_5_out[3], out_20, xor_4_out);
  and and_11 (and_11_out, xor_4_out, out_20);
  or or_2 (C0_out, and_8_out, and_2_out);
  or or_3 (out_20, and_10_out, and_3_out);
  or or_4 (C3_out, and_11_out, and_4_out);
  LED led_2 (.in(xor_5_out[2]));
  LED led_3 (.in(xor_5_out[3]));
  // Probe on xor_5_out[0]
  // Probe on xor_5_out[1]
  or or_5 (C1_out, and_9_out, and_5_out);
  // Probe on xor_5_out[2]
  xor xor_9 (out_17, in_7, in_8);
  LED led_4 (.in(xor_5_out[1]));
  LED led_5 (.in(xor_5_out[0]));
  // Probe on xor_5_out[3]
  // Probe on xor_5_out

  // Other names for the same wires on the sheet: C_in = Selector

  // Notes on the sheet:
  //   IF SEL==0 ADD
  //   IF SEL==1 SUB
  //   Overflow
  //   Kakey Fon
  //   MAC295
  //   a3
  //   B
  //   A0
  //   B0
  //   B1
  //   A2
  //   B2
  //   A3
  //   B3
  //   A1
  //   S0
  //   C0
  //   S1
  //   C1
  //   S2
  //   C2
  //   S3
  //   C3
  //   4 Bits Adder/Subtractor in Binary 
  //   The limit for 4 bits binary
  //   S0
  //   C0
  //   S1
  //   C1
  //   S2
  //   C2
  //   S3
  //   C3
  //   Answers in LED
  //   R0
  //   S
  //   R1
  //   R2
  //   C2 out 
  //   R3
  //   Answers in Binary #
endmodule
