// Logisim project MuxDataTransferDLATCHES.circ as structural Verilog: 1 circuit, main circuit main
module main (
  input  in_1,
  input  source_A,
  input  in_3,
  input  in_4,
  input  Source_B,
  input  in_6,
  input  in_7,
  input  in_8
);

  wire button_1_out, d_ff_7_q, d_ff_8_q, d_ff_9_q, d_ff_10_q, d_ff_11_q, d_ff_12_q;
  wire [2:0] d_ff_1_q, d_ff_4_q, demultiplexer_1_out0, demultiplexer_1_out1, multiplexer_1_out;

  Button button_1 (.out(button_1_out));
  D_Flip_Flop d_ff_1 (.clk(button_1_out), .D(in_1), .Q(d_ff_1_q[0]));  // open: Qn, preset, en, reset
  D_Flip_Flop d_ff_2 (.clk(button_1_out), .D(source_A), .Q(d_ff_1_q[1]));  // open: Qn, preset, en, reset
  D_Flip_Flop d_ff_3 (.clk(button_1_out), .D(in_3), .Q(d_ff_1_q[2]));  // open: Qn, preset, en, reset
  D_Flip_Flop d_ff_4 (.clk(button_1_out), .D(in_4), .Q(d_ff_4_q[0]));  // open: Qn, preset, en, reset
  D_Flip_Flop d_ff_5 (.clk(button_1_out), .D(Source_B), .Q(d_ff_4_q[1]));  // open: Qn, preset, en, reset
  D_Flip_Flop d_ff_6 (.clk(button_1_out), .D(in_8), .Q(d_ff_4_q[2]));  // open: Qn, preset, en, reset
  Multiplexer #(.width(3), .enable("false")) multiplexer_1 (
    .in0(d_ff_1_q), .in1(d_ff_4_q), .out(multiplexer_1_out), .sel(in_6));
  Demultiplexer #(.width(3), .enable("false")) demultiplexer_1 (
    .out0(demultiplexer_1_out0), .out1(demultiplexer_1_out1), .in(multiplexer_1_out), .sel(in_7));
  D_Flip_Flop d_ff_7 (.clk(button_1_out), .D(demultiplexer_1_out0[0]), .Q(d_ff_7_q));  // open: Qn, preset, en, reset
  D_Flip_Flop d_ff_8 (.clk(button_1_out), .D(demultiplexer_1_out0[1]), .Q(d_ff_8_q));  // open: Qn, preset, en, reset
  D_Flip_Flop d_ff_9 (.clk(button_1_out), .D(demultiplexer_1_out0[2]), .Q(d_ff_9_q));  // open: Qn, preset, en, reset
  D_Flip_Flop d_ff_10 (.clk(button_1_out), .D(demultiplexer_1_out1[0]), .Q(d_ff_10_q));  // open: Qn, preset, en, reset
  D_Flip_Flop d_ff_11 (.clk(button_1_out), .D(demultiplexer_1_out1[1]), .Q(d_ff_11_q));  // open: Qn, preset, en, reset
  D_Flip_Flop d_ff_12 (.clk(button_1_out), .D(demultiplexer_1_out1[2]), .Q(d_ff_12_q));  // open: Qn, preset, en, reset
  LED led_1 (.in(d_ff_7_q));
  LED led_2 (.in(d_ff_8_q));
  LED led_3 (.in(d_ff_9_q));
  LED led_4 (.in(d_ff_10_q));
  LED led_5 (.in(d_ff_11_q));
  LED led_6 (.in(d_ff_12_q));

  // Notes on the sheet:
  //   Capture and transfer data
  //   Source              Destination
  //   Desitnation C
  //   Destination D
endmodule
