// Logisim project classlab.circ as structural Verilog: 1 circuit, main circuit main
module main (
  input  in_1,
  input  source_A,
  input  in_3,
  input  in_4,
  input  Source_B,
  input  [1:0] in_6,
  input  in_7,
  input  in_8,
  input  in_9,
  input  in_10,
  input  in_11,
  input  source_D,
  input  in_13,
  input  in_14
);

  wire button_1_out, d_ff_13_q, d_ff_14_q, d_ff_15_q, d_ff_16_q, d_ff_17_q, d_ff_18_q;
  wire [2:0] d_ff_1_q, d_ff_4_q, d_ff_7_q, d_ff_10_q, demultiplexer_1_out0, demultiplexer_1_out1,
       multiplexer_1_out;

  Button button_1 (.out(button_1_out));
  D_Flip_Flop d_ff_1 (.clk(button_1_out), .D(in_1), .Q(d_ff_1_q[0]));  // open: Qn, preset, en, reset
  D_Flip_Flop d_ff_2 (.clk(button_1_out), .D(source_A), .Q(d_ff_1_q[1]));  // open: Qn, preset, en, reset
  D_Flip_Flop d_ff_3 (.clk(button_1_out), .D(in_3), .Q(d_ff_1_q[2]));  // open: Qn, preset, en, reset
  D_Flip_Flop d_ff_4 (.clk(button_1_out), .D(in_4), .Q(d_ff_4_q[0]));  // open: Qn, preset, en, reset
  D_Flip_Flop d_ff_5 (.clk(button_1_out), .D(Source_B), .Q(d_ff_4_q[1]));  // open: Qn, preset, en, reset
  D_Flip_Flop d_ff_6 (.clk(button_1_out), .D(in_8), .Q(d_ff_4_q[2]));  // open: Qn, preset, en, reset
  D_Flip_Flop d_ff_7 (.clk(button_1_out), .D(in_9), .Q(d_ff_7_q[0]));  // open: Qn, preset, en, reset
  D_Flip_Flop d_ff_8 (.clk(button_1_out), .D(in_10), .Q(d_ff_7_q[1]));  // open: Qn, preset, en, reset
  D_Flip_Flop d_ff_9 (.clk(button_1_out), .D(in_11), .Q(d_ff_7_q[2]));  // open: Qn, preset, en, reset
  D_Flip_Flop d_ff_10 (.clk(button_1_out), .D(source_D), .Q(d_ff_10_q[0]));  // open: Qn, preset, en, reset
  D_Flip_Flop d_ff_11 (.clk(button_1_out), .D(in_13), .Q(d_ff_10_q[1]));  // open: Qn, preset, en, reset
  D_Flip_Flop d_ff_12 (.clk(button_1_out), .D(in_14), .Q(d_ff_10_q[2]));  // open: Qn, preset, en, reset
  Demultiplexer #(.width(3), .enable("false")) demultiplexer_1 (
    .out0(demultiplexer_1_out0), .out1(demultiplexer_1_out1), .in(multiplexer_1_out), .sel(in_7));
  Multiplexer #(.select(2), .width(3), .enable("false")) multiplexer_1 (
    .in0(d_ff_1_q), .in1(d_ff_4_q), .in2(d_ff_7_q), .in3(d_ff_10_q), .out(multiplexer_1_out), .sel(in_6));
  D_Flip_Flop d_ff_13 (.clk(button_1_out), .D(demultiplexer_1_out0[0]), .Q(d_ff_13_q));  // open: Qn, preset, en, reset
  D_Flip_Flop d_ff_14 (.clk(button_1_out), .D(demultiplexer_1_out0[1]), .Q(d_ff_14_q));  // open: Qn, preset, en, reset
  D_Flip_Flop d_ff_15 (.clk(button_1_out), .D(demultiplexer_1_out0[2]), .Q(d_ff_15_q));  // open: Qn, preset, en, reset
  D_Flip_Flop d_ff_16 (.clk(button_1_out), .D(demultiplexer_1_out1[0]), .Q(d_ff_16_q));  // open: Qn, preset, en, reset
  D_Flip_Flop d_ff_17 (.clk(button_1_out), .D(demultiplexer_1_out1[1]), .Q(d_ff_17_q));  // open: Qn, preset, en, reset
  D_Flip_Flop d_ff_18 (.clk(button_1_out), .D(demultiplexer_1_out1[2]), .Q(d_ff_18_q));  // open: Qn, preset, en, reset
  LED led_1 (.in(d_ff_13_q));
  LED led_2 (.in(d_ff_14_q));
  LED led_3 (.in(d_ff_15_q));
  LED led_4 (.in(d_ff_16_q));
  LED led_5 (.in(d_ff_17_q));
  LED led_6 (.in(d_ff_18_q));

  // Notes on the sheet:
  //   Kakey Fon
  //   source C
  //   Capture and transfer data
  //   00
  //   Source              Destination
  //   Machine code
  //   00
  //   0
  //   01
  //   1
  //   01
  //   0
  //   10
  //   1
  //   10
  //   11
  //   0
  //   11
  //   1
  //   0
  //   1
  //   source  A -> destionation A
  //   source A -> destionation B
  //   source B -> destionation A
  //   source B -> destionation B
  //   soucer C -> destionation A
  //   source C -> destionation B
  //   source D -> destionation A
  //   source D -> destionation B
  //   Desitnation A
  //   Destination B
endmodule
