// Logisim project withoutXOR.circ as structural Verilog: 1 circuit, main circuit main
module main (
  input  A,
  input  in_2,
  input  in_3,
  input  in_4,
  input  [3:0] in_5,
  input  b3,
  input  b2,
  input  b1,
  input  b0,
  input  [3:0] in_10,
  input  Selector,
  output c0,
  output c1,
  output c2,
  output c3
);

  wire and_1_out, and_2_out, and_3_out, and_4_out, and_5_out, and_6_out, and_7_out, and_8_out, and_9_out,
       and_10_out, and_11_out, and_12_out, and_13_out, and_14_out, and_15_out, and_16_out, and_17_out,
       and_18_out, and_19_out, and_20_out, and_21_out, and_22_out, and_23_out, and_24_out, and_25_out,
       not_1_out, not_3_out, not_4_out, not_5_out, not_6_out, not_7_out, not_8_out, not_9_out, not_10_out,
       not_11_out, not_12_out, not_13_out, not_14_out, not_15_out, not_16_out, not_17_out, not_18_out,
       or_1_out, or_2_out, or_7_out, or_10_out;
  wire [3:0] multiplexer_1_out, not_2_out, or_3_out;

  LED led_1 (.in(and_1_out));
  and and_1 (and_1_out, not_1_out, c3);
  not not_1 (not_1_out, Selector);
  assign not_2_out = ~in_10;  // NOT_Gate not_2, 4 bits wide
  Multiplexer #(.width(4), .enable("false")) multiplexer_1 (
    .in0(in_10), .in1(not_2_out), .out(multiplexer_1_out), .sel(Selector));
  not not_3 (not_3_out, in_5[0]);
  not not_4 (not_4_out, multiplexer_1_out[0]);
  and and_2 (and_2_out, in_5[0], multiplexer_1_out[0]);
  and and_3 (and_3_out, not_3_out, multiplexer_1_out[0]);
  and and_4 (and_4_out, in_5[0], not_4_out);
  or or_1 (or_1_out, and_3_out, and_4_out);
  not not_5 (not_5_out, in_5[1]);
  and and_5 (and_5_out, not_5_out, multiplexer_1_out[1]);
  and and_6 (and_6_out, in_5[1], not_6_out);
  not not_6 (not_6_out, multiplexer_1_out[1]);
  and and_7 (and_7_out, in_5[1], multiplexer_1_out[1]);
  not not_7 (not_7_out, Selector);
  not not_8 (not_8_out, or_1_out);
  or or_2 (or_2_out, and_5_out, and_6_out);
  and and_8 (and_8_out, not_7_out, or_1_out);
  and and_9 (and_9_out, Selector, not_8_out);
  and and_10 (and_10_out, or_1_out, Selector);
  // Probe on or_3_out[0]
  or or_3 (or_3_out[0], and_8_out, and_9_out);
  or or_4 (c0, and_10_out, and_2_out);
  not not_9 (not_9_out, c0);
  not not_10 (not_10_out, or_2_out);
  not not_11 (not_11_out, in_5[2]);
  not not_12 (not_12_out, multiplexer_1_out[2]);
  and and_11 (and_11_out, in_5[2], multiplexer_1_out[2]);
  and and_12 (and_12_out, not_9_out, or_2_out);
  and and_13 (and_13_out, c0, not_10_out);
  and and_14 (and_14_out, or_2_out, c0);
  and and_15 (and_15_out, not_11_out, multiplexer_1_out[2]);
  and and_16 (and_16_out, in_5[2], not_12_out);
  or or_5 (or_3_out[1], and_12_out, and_13_out);
  // Probe on or_3_out[1]
  or or_6 (c1, and_14_out, and_7_out);
  or or_7 (or_7_out, and_15_out, and_16_out);
  not not_13 (not_13_out, c1);
  not not_14 (not_14_out, or_7_out);
  not not_15 (not_15_out, in_5[3]);
  not not_16 (not_16_out, multiplexer_1_out[3]);
  and and_17 (and_17_out, in_5[3], multiplexer_1_out[3]);
  and and_18 (and_18_out, not_13_out, or_7_out);
  and and_19 (and_19_out, c1, not_14_out);
  and and_20 (and_20_out, or_7_out, c1);
  and and_21 (and_21_out, not_15_out, multiplexer_1_out[3]);
  and and_22 (and_22_out, in_5[3], not_16_out);
  or or_8 (or_3_out[2], and_18_out, and_19_out);
  or or_9 (c2, and_20_out, and_11_out);
  or or_10 (or_10_out, and_21_out, and_22_out);
  // Probe on or_3_out[2]
  LED led_2 (.in(or_3_out[0]));
  LED led_3 (.in(or_3_out[1]));
  LED led_4 (.in(or_3_out[2]));
  LED led_5 (.in(or_3_out[3]));
  not not_17 (not_17_out, c2);
  not not_18 (not_18_out, or_10_out);
  and and_23 (and_23_out, not_17_out, or_10_out);
  and and_24 (and_24_out, c2, not_18_out);
  and and_25 (and_25_out, or_10_out, c2);
  or or_11 (or_3_out[3], and_23_out, and_24_out);
  // Probe on or_3_out[3]
  or or_12 (c3, and_25_out, and_17_out);
  // Probe on or_3_out

  // Notes on the sheet:
  //   Kakey Fon
  //   MAC295
  //   B
  //   IF SEL==0 ADD
  //   IF SEL==1 SUB
  //   Sum A0+B0
  //   Sum A1+B1
  //   Sum
  //   Sum A2+B2
  //   S0
  //   Sum
  //   4 Bits Adder/Subtractor in Binary 
  //   S1
  //   Sum
  //   The limit for the binary
  //   Sum A3+B3
  //   S2
  //   Answers in LED
  //   Sum
  //   Answers in Binary #
  //   s3
endmodule
